// Logisim project CPUComplexGajewskiGierlak.circ as structural Verilog: 2 circuits, main circuit CPU
module CPU (
);

  wire AccImE, AccImS, AccReE, AccReS, CPUclk_out, CS_iar_e, CS_iar_s, CS_ir_s, CS_mar_s, CS_r0_e, CS_r0_s,
       CS_r1_e, CS_r1_s, CS_r2_e, CS_r2_s, CS_r3_e, CS_r3_s, CS_r4_e, CS_r4_s, CS_r5_e, CS_r5_s, CS_r6_e,
       CS_r6_s, CS_r7_e, CS_r7_s, CS_ram_e, CS_ram_s, CS_rstflg, CS_setflg, IarTmpE, IarTmpS, ImOvE, ReOvE,
       TMPB_S, TMPC_S, TMPD_S;
  wire [3:0] CS_alu;
  wire [6:0] alu_v2_1_div_by_0, FLAGS_q;
  wire [10:0] ACC_IM_q, ACC_RE_q, alu_v2_1_high_bits_imag, alu_v2_1_high_bits_real, alu_v2_1_result_a,
       alu_v2_1_result_b, controlled_buffer_1_out, IAR_q, IarIncTmp_q, Im_OV_q, IR_q, MAR_S_out, RAM_dout,
       Re_OV_q, Reg000_q, Reg001_q, Reg010_q, Reg011_q, Reg100_q, Reg101_q, Reg110_q, Reg111_q, TempB_q,
       TempC_q, TempD_q;

  Clock sysclk ();  // open: out
  Clock CPUclk (.out(CPUclk_out));
  Register #(.width(11)) TempB (.D(controlled_buffer_1_out), .en(TMPB_S), .clk(CPUclk_out), .Q(TempB_q));  // open: clr
  Register #(.width(11)) Re_OV (.D(alu_v2_1_high_bits_real), .clk(CPUclk_out), .Q(Re_OV_q));  // open: en, clr
  Register #(.width(11)) Im_OV (.D(alu_v2_1_high_bits_imag), .clk(CPUclk_out), .Q(Im_OV_q));  // open: en, clr
  assign controlled_buffer_1_out = ReOvE ? Re_OV_q : 11'bz;  // Controlled_Buffer controlled_buffer_1
  assign controlled_buffer_1_out = ImOvE ? Im_OV_q : 11'bz;  // Controlled_Buffer controlled_buffer_2
  ALU_v2 alu_v2_1 (
    .A(controlled_buffer_1_out), .B(TempB_q), .C(TempC_q), .D(TempD_q), .OPERATION(CS_alu),
    .CIN_IM(FLAGS_q[6]), .CIN_RE(FLAGS_q[5]), .RESULT_A(alu_v2_1_result_a), .RESULT_B(alu_v2_1_result_b),
    .COUT_RE(alu_v2_1_div_by_0[5]), .COUT_IM(alu_v2_1_div_by_0[6]), .DIV_BY_0(alu_v2_1_div_by_0[0]),
    .isZeroInAFlag(alu_v2_1_div_by_0[4]), .AequalsCFLAG(alu_v2_1_div_by_0[1]),
    .AisHigherThanCFLAG(alu_v2_1_div_by_0[2]), .A_B_equals_C_D(alu_v2_1_div_by_0[3]),
    .HIGH_BITS_REAL(alu_v2_1_high_bits_real), .HIGH_BITS_IMAG(alu_v2_1_high_bits_imag));
  Register #(.width(11)) TempC (.D(controlled_buffer_1_out), .en(TMPC_S), .clk(CPUclk_out), .Q(TempC_q));  // open: clr
  Register #(.width(11)) ACC_IM (.D(alu_v2_1_result_b), .en(AccImS), .clk(CPUclk_out), .Q(ACC_IM_q));  // open: clr
  Register #(.width(11)) ACC_RE (.D(alu_v2_1_result_a), .en(AccReS), .clk(CPUclk_out), .Q(ACC_RE_q));  // open: clr
  Register #(.width(11)) IarIncTmp (
    .D(alu_v2_1_result_a), .en(IarTmpS), .clk(CPUclk_out), .Q(IarIncTmp_q));  // open: clr
  assign controlled_buffer_1_out = IarTmpE ? IarIncTmp_q : 11'bz;  // Controlled_Buffer controlled_buffer_3
  Register #(.width(11)) TempD (.D(controlled_buffer_1_out), .en(TMPD_S), .clk(CPUclk_out), .Q(TempD_q));  // open: clr
  Register #(.width(7)) FLAGS (.D(alu_v2_1_div_by_0), .en(CS_setflg), .clk(CPUclk_out), .Q(FLAGS_q), .clr(CS_rstflg));
  assign controlled_buffer_1_out = AccImE ? ACC_IM_q : 11'bz;  // Controlled_Buffer controlled_buffer_4
  assign controlled_buffer_1_out = AccReE ? ACC_RE_q : 11'bz;  // Controlled_Buffer controlled_buffer_5
  Register #(.width(11)) Reg000 (
    .D(controlled_buffer_1_out), .en(CS_r0_s), .clk(CPUclk_out), .Q(Reg000_q));  // open: clr
  Register #(.width(11)) Reg001 (
    .D(controlled_buffer_1_out), .en(CS_r1_s), .clk(CPUclk_out), .Q(Reg001_q));  // open: clr
  assign controlled_buffer_1_out = CS_r0_e ? Reg000_q : 11'bz;  // Controlled_Buffer controlled_buffer_6
  Register #(.width(11)) Reg010 (
    .D(controlled_buffer_1_out), .en(CS_r2_s), .clk(CPUclk_out), .Q(Reg010_q));  // open: clr
  assign controlled_buffer_1_out = CS_r1_e ? Reg001_q : 11'bz;  // Controlled_Buffer controlled_buffer_7
  assign controlled_buffer_1_out = CS_r2_e ? Reg010_q : 11'bz;  // Controlled_Buffer controlled_buffer_8
  Register #(.width(11)) IAR (.D(controlled_buffer_1_out), .en(CS_iar_s), .clk(CPUclk_out), .Q(IAR_q));  // open: clr
  Register #(.width(11)) Reg011 (
    .D(controlled_buffer_1_out), .en(CS_r3_s), .clk(CPUclk_out), .Q(Reg011_q));  // open: clr
  assign controlled_buffer_1_out = CS_iar_e ? IAR_q : 11'bz;  // Controlled_Buffer controlled_buffer_9
  assign controlled_buffer_1_out = CS_r3_e ? Reg011_q : 11'bz;  // Controlled_Buffer controlled_buffer_10
  Register #(.width(11)) IR (.D(controlled_buffer_1_out), .en(CS_ir_s), .clk(CPUclk_out), .Q(IR_q));  // open: clr
  Register #(.width(11)) Reg100 (
    .D(controlled_buffer_1_out), .en(CS_r4_s), .clk(CPUclk_out), .Q(Reg100_q));  // open: clr
  Register #(.width(11)) Reg101 (
    .D(controlled_buffer_1_out), .en(CS_r5_s), .clk(CPUclk_out), .Q(Reg101_q));  // open: clr
  assign controlled_buffer_1_out = CS_r4_e ? Reg100_q : 11'bz;  // Controlled_Buffer controlled_buffer_11
  Register #(.width(11)) Reg110 (
    .D(controlled_buffer_1_out), .en(CS_r6_s), .clk(CPUclk_out), .Q(Reg110_q));  // open: clr
  assign controlled_buffer_1_out = CS_r5_e ? Reg101_q : 11'bz;  // Controlled_Buffer controlled_buffer_12
  CS CS (
    .clk(CPUclk_out), .RAM_E(CS_ram_e), .AccReE(AccReE), .R0_E(CS_r0_e), .R1_E(CS_r1_e), .R2_E(CS_r2_e),
    .R3_E(CS_r3_e), .ALU(CS_alu), .MAR_S(CS_mar_s), .AccReS(AccReS), .RAM_S(CS_ram_s), .TMPC_S(TMPC_S),
    .R0_S(CS_r0_s), .R1_S(CS_r1_s), .R2_S(CS_r2_s), .R3_S(CS_r3_s), .IR_input(IR_q), .IAR_E(CS_iar_e),
    .IR_S(CS_ir_s), .IAR_S(CS_iar_s), .R4_E(CS_r4_e), .R5_E(CS_r5_e), .R6_E(CS_r6_e), .R7_E(CS_r7_e),
    .R4_S(CS_r4_s), .R5_S(CS_r5_s), .R6_S(CS_r6_s), .R7_S(CS_r7_s), .TMPB_S(TMPB_S), .AccImE(AccImE),
    .TMPD_S(TMPD_S), .IarIncE(IarTmpE), .IarIncS(IarTmpS), .ReOvE(ReOvE), .ImOvE(ImOvE),
    .DIV_BY_0(FLAGS_q[0]), .A_equ_C(FLAGS_q[1]), .A_bigger_C(FLAGS_q[2]), .Complex_equ(FLAGS_q[3]),
    .A_is_0(FLAGS_q[4]), .SetFlg(CS_setflg), .RstFlg(CS_rstflg), .AccImS(AccImS));
  assign controlled_buffer_1_out = CS_r6_e ? Reg110_q : 11'bz;  // Controlled_Buffer controlled_buffer_13
  Register #(.width(11)) Reg111 (
    .D(controlled_buffer_1_out), .en(CS_r7_s), .clk(CPUclk_out), .Q(Reg111_q));  // open: clr
  assign controlled_buffer_1_out = CS_r7_e ? Reg111_q : 11'bz;  // Controlled_Buffer controlled_buffer_14
  assign MAR_S_out = CS_mar_s ? controlled_buffer_1_out : 11'bz;  // Controlled_Buffer MAR_S
  RAM #(.addrWidth(11), .dataWidth(11), .databus("bibus")) RAM (
    .addr(MAR_S_out), .we(CS_ram_s), .clk(CPUclk_out), .din(controlled_buffer_1_out), .dout(RAM_dout));  // open: oe
  assign controlled_buffer_1_out = CS_ram_e ? RAM_dout : 11'bz;  // Controlled_Buffer RAM_E

  // Notes on the sheet:
  //   Overflow registers
  //   Register what serves
  //   to increase IAR
  //   Registers to hold arguments before ALU operation
  //   Accumulators for
  //   imaginary and real 
  //   ALU results
  //   Random access registers
endmodule

module CS (
  input  clk,
  input  [10:0] IR_input,
  input  DIV_BY_0,
  input  A_equ_C,
  input  A_bigger_C,
  input  Complex_equ,
  input  A_is_0,
  output RAM_E,
  output IAR_E,
  output AccReE,
  output AccImE,
  output IarIncS,
  output IarIncE,
  output ReOvE,
  output MAR_S,
  output ImOvE,
  output SetFlg,
  output AccReS,
  output RstFlg,
  output AccImS,
  output RAM_S,
  output TMPC_S,
  output TMPB_S,
  output TMPD_S,
  output IR_S,
  output IAR_S,
  output R0_E,
  output R1_E,
  output R0_S,
  output R1_S,
  output R2_E,
  output R2_S,
  output R3_E,
  output R3_S,
  output R4_S,
  output R4_E,
  output R5_S,
  output R5_E,
  output R6_S,
  output R6_E,
  output R7_S,
  output R7_E,
  output [3:0] ALU
);

  wire ADD_1_DATA, and_2_out, and_3_out, and_4_out, and_5_out, and_6_out, and_7_out, and_8_out, and_9_out,
       and_10_out, and_11_out, and_12_out, and_13_out, and_14_out, and_15_out, and_16_out, and_17_out,
       and_18_out, and_19_out, and_20_out, and_21_out, and_22_out, and_25_out, and_26_out, and_27_out,
       and_28_out, and_29_out, and_30_out, and_31_out, and_32_out, and_33_out, and_34_out, and_35_out,
       and_36_out, and_37_out, and_38_out, and_39_out, and_40_out, DATA, decoder_2_out0, decoder_2_out1,
       decoder_2_out2, decoder_2_out3, decoder_2_out4, decoder_2_out5, decoder_2_out6, decoder_2_out7,
       decoder_3_out0, decoder_3_out1, decoder_3_out2, decoder_3_out3, decoder_3_out4, decoder_3_out5,
       decoder_3_out6, decoder_3_out7, decoder_4_out0, decoder_5_out0, decoder_6_out5, decoder_7_out0,
       decoder_7_out1, decoder_7_out2, decoder_7_out3, decoder_7_out4, decoder_7_out5, decoder_7_out6,
       decoder_7_out7, decoder_8_out0, decoder_8_out1, decoder_8_out2, decoder_8_out3, decoder_8_out4,
       decoder_8_out5, decoder_8_out6, decoder_8_out7, FLAG_IS_SET, IAR_TMP_S, JMPR, JUMP, JUMP_IF, LOAD,
       not_1_out, or_9_out, or_10_out, REGA_E, REGA_S, REGB_E, REGB_S, SET_IM, STEP_2, STEP_3, STEP_4,
       STEP_5, STEP_6, STORE, STORE_OVs, STORE_RESULTS, xnor_1_out;
  wire [3:0] controlled_buffer_2_out, controlled_buffer_11_out, controlled_buffer_19_out, counter_1_q;
  wire [7:0] controlled_buffer_12_out, ROM_data;

  or or_1 (R0_E, and_2_out, and_10_out);
  or or_2 (R1_E, and_3_out, and_11_out);
  or or_3 (R2_E, and_4_out, and_12_out);
  or or_4 (R3_E, and_5_out, and_13_out);
  or or_5 (R4_E, and_6_out, and_14_out);
  or or_6 (R5_E, and_7_out, and_15_out);
  or or_7 (R6_E, and_8_out, and_16_out);
  or or_8 (R7_E, and_9_out, and_17_out);
  assign ALU = or_9_out ? 4'b1000 : 4'bz;  // Controlled_Buffer controlled_buffer_1
  or or_9 (or_9_out, IAR_TMP_S, ADD_1_DATA);
  assign controlled_buffer_2_out = IR_input[10] ? 4'b0000 : 4'bz;  // Controlled_Buffer controlled_buffer_2
  assign controlled_buffer_2_out = STORE ? 4'b0010 : 4'bz;  // Controlled_Buffer controlled_buffer_3
  assign controlled_buffer_2_out = DATA ? 4'b0011 : 4'bz;  // Controlled_Buffer controlled_buffer_4
  assign controlled_buffer_2_out = JMPR ? 4'b0100 : 4'bz;  // Controlled_Buffer controlled_buffer_5
  assign controlled_buffer_2_out = or_10_out ? 4'b0101 : 4'bz;  // Controlled_Buffer controlled_buffer_6
  or or_10 (or_10_out, JUMP, JUMP_IF);
  assign controlled_buffer_2_out = SET_IM ? 4'b0110 : 4'bz;  // Controlled_Buffer controlled_buffer_7
  assign controlled_buffer_2_out = STORE_RESULTS ? 4'b0111 : 4'bz;  // Controlled_Buffer controlled_buffer_8
  assign controlled_buffer_2_out = STORE_OVs ? 4'b1000 : 4'bz;  // Controlled_Buffer controlled_buffer_9
  assign controlled_buffer_2_out = LOAD ? 4'b0001 : 4'bz;  // Controlled_Buffer controlled_buffer_10
  Counter #(.width(4), .max('ha)) counter_1 (.clk(clk), .Q(counter_1_q));  // open: clr, load, up, count, D, carry
  and and_1 (ADD_1_DATA, STEP_4, DATA);
  and and_2 (and_2_out, REGB_E, decoder_2_out0);
  and and_3 (and_3_out, REGB_E, decoder_2_out1);
  and and_4 (and_4_out, REGB_E, decoder_2_out2);
  and and_5 (and_5_out, REGB_E, decoder_2_out3);
  and and_6 (and_6_out, REGB_E, decoder_2_out4);
  and and_7 (and_7_out, REGB_E, decoder_2_out5);
  and and_8 (and_8_out, REGB_E, decoder_2_out6);
  and and_9 (and_9_out, REGB_E, decoder_2_out7);
  and and_10 (and_10_out, REGA_E, decoder_3_out0);
  and and_11 (and_11_out, REGA_E, decoder_3_out1);
  and and_12 (and_12_out, REGA_E, decoder_3_out2);
  and and_13 (and_13_out, REGA_E, decoder_3_out3);
  and and_14 (and_14_out, REGA_E, decoder_3_out4);
  and and_15 (and_15_out, REGA_E, decoder_3_out5);
  and and_16 (and_16_out, REGA_E, decoder_3_out6);
  and and_17 (and_17_out, REGA_E, decoder_3_out7);
  assign controlled_buffer_11_out = STEP_6 ? 4'b0011 : 4'bz;  // Controlled_Buffer controlled_buffer_11
  or or_11 (FLAG_IS_SET, and_18_out, and_19_out, and_20_out, and_21_out, and_22_out);
  assign controlled_buffer_12_out = IAR_TMP_S ? {8{1'b0}} : 8'bz;  // Controlled_Buffer controlled_buffer_12
  assign controlled_buffer_11_out = STEP_4 ? 4'b0001 : 4'bz;  // Controlled_Buffer controlled_buffer_13
  assign controlled_buffer_11_out = STEP_5 ? 4'b0010 : 4'bz;  // Controlled_Buffer controlled_buffer_14
  assign ALU = STEP_6 ? controlled_buffer_19_out : 4'bz;  // Controlled_Buffer controlled_buffer_15
  and and_18 (and_18_out, DIV_BY_0, IR_input[4]);
  and and_19 (and_19_out, A_equ_C, IR_input[3]);
  and and_20 (and_20_out, A_bigger_C, IR_input[2]);
  and and_21 (and_21_out, Complex_equ, IR_input[1]);
  and and_22 (and_22_out, A_is_0, IR_input[0]);
  Decoder #(.select(4)) decoder_1 (
    .out0(IAR_TMP_S), .out2(STEP_2), .out4(STEP_3), .out6(STEP_4), .out8(STEP_5), .out10(STEP_6),
    .sel(counter_1_q));  // open: out1, out3, out5, out7, out9, out11, out12, out13, out14, out15, en
  assign controlled_buffer_12_out = STEP_2 ? 8'h1 : 8'bz;  // Controlled_Buffer controlled_buffer_16
  assign controlled_buffer_12_out = STEP_3 ? 8'h2 : 8'bz;  // Controlled_Buffer controlled_buffer_17
  assign controlled_buffer_12_out = xnor_1_out ? {controlled_buffer_11_out, controlled_buffer_2_out} : 8'bz;  // Controlled_Buffer controlled_buffer_18
  NotExactlyOne xnor_1 (.out(xnor_1_out), .in0(IAR_TMP_S), .in1(STEP_2), .in2(STEP_3));
  Decoder #(.select(3)) decoder_2 (
    .out0(decoder_2_out0), .out1(decoder_2_out1), .out2(decoder_2_out2), .out3(decoder_2_out3),
    .out4(decoder_2_out4), .out5(decoder_2_out5), .out6(decoder_2_out6), .out7(decoder_2_out7),
    .sel(IR_input[2:0]));  // open: en
  Decoder #(.select(3)) decoder_3 (
    .out0(decoder_3_out0), .out1(decoder_3_out1), .out2(decoder_3_out2), .out3(decoder_3_out3),
    .out4(decoder_3_out4), .out5(decoder_3_out5), .out6(decoder_3_out6), .out7(decoder_3_out7),
    .sel(IR_input[5:3]));  // open: en
  and and_23 (SetFlg, STEP_6, IR_input[10]);
  ROM ROM (.addr(controlled_buffer_12_out), .data(ROM_data));
  assign controlled_buffer_19_out = IR_input[10] ? IR_input[9:6] : 4'bz;  // Controlled_Buffer controlled_buffer_19
  Decoder #(.select(4)) decoder_4 (
    .out0(decoder_4_out0), .out1(RAM_E), .out2(IAR_E), .out3(REGA_E), .out4(REGB_E), .out5(AccReE),
    .out6(IarIncE), .out7(AccImE), .out8(ReOvE), .out9(ImOvE), .sel(ROM_data[7:4]));  // open: out10, out11, out12, out13, out14, out15, en
  Decoder #(.select(4)) decoder_5 (
    .out0(decoder_5_out0), .out1(IR_S), .out2(MAR_S), .out3(AccImS), .out4(TMPC_S), .out5(REGB_S),
    .out6(IAR_S), .out7(RAM_S), .out8(TMPB_S), .out9(TMPD_S), .out10(REGA_S), .sel(ROM_data[3:0]));  // open: out11, out12, out13, out14, out15, en
  not not_1 (not_1_out, IR_input[10]);
  Decoder #(.select(4)) decoder_6 (
    .out0(LOAD), .out1(STORE), .out2(DATA), .out3(JMPR), .out4(JUMP), .out5(decoder_6_out5), .out6(SET_IM),
    .out7(STORE_RESULTS), .out8(RstFlg), .out9(STORE_OVs), .sel(IR_input[9:6]), .en(not_1_out));  // open: out10, out11, out12, out13, out14, out15
  and and_24 (JUMP_IF, decoder_6_out5, FLAG_IS_SET);
  or or_12 (IarIncS, IAR_TMP_S, ADD_1_DATA);
  Decoder #(.select(3)) decoder_7 (
    .out0(decoder_7_out0), .out1(decoder_7_out1), .out2(decoder_7_out2), .out3(decoder_7_out3),
    .out4(decoder_7_out4), .out5(decoder_7_out5), .out6(decoder_7_out6), .out7(decoder_7_out7),
    .sel(IR_input[2:0]));  // open: en
  Decoder #(.select(3)) decoder_8 (
    .out0(decoder_8_out0), .out1(decoder_8_out1), .out2(decoder_8_out2), .out3(decoder_8_out3),
    .out4(decoder_8_out4), .out5(decoder_8_out5), .out6(decoder_8_out6), .out7(decoder_8_out7),
    .sel(IR_input[5:3]));  // open: en
  and and_25 (and_25_out, decoder_7_out0, REGB_S);
  and and_26 (and_26_out, decoder_7_out1, REGB_S);
  and and_27 (and_27_out, decoder_7_out2, REGB_S);
  and and_28 (and_28_out, decoder_7_out3, REGB_S);
  and and_29 (and_29_out, decoder_7_out4, REGB_S);
  and and_30 (and_30_out, decoder_7_out5, REGB_S);
  and and_31 (and_31_out, decoder_7_out6, REGB_S);
  and and_32 (and_32_out, decoder_7_out7, REGB_S);
  and and_33 (and_33_out, decoder_8_out0, REGA_S);
  and and_34 (and_34_out, decoder_8_out1, REGA_S);
  and and_35 (and_35_out, decoder_8_out2, REGA_S);
  and and_36 (and_36_out, decoder_8_out3, REGA_S);
  and and_37 (and_37_out, decoder_8_out4, REGA_S);
  and and_38 (and_38_out, decoder_8_out5, REGA_S);
  and and_39 (and_39_out, decoder_8_out6, REGA_S);
  and and_40 (and_40_out, decoder_8_out7, REGA_S);
  or or_13 (R0_S, and_25_out, and_33_out);
  or or_14 (R1_S, and_26_out, and_34_out);
  or or_15 (R2_S, and_27_out, and_35_out);
  or or_16 (R3_S, and_28_out, and_36_out);
  or or_17 (R4_S, and_29_out, and_37_out);
  or or_18 (R5_S, and_30_out, and_38_out);
  or or_19 (R6_S, and_31_out, and_39_out);
  or or_20 (R7_S, and_32_out, and_40_out);

  assign AccReS = AccImS;

  // Other names for the same wires on the sheet: ACCim_E = AccImE; ACCre_E = AccReE; ACCim_S = AccImS;
  //   ACCre_S = AccImS; IAR_TMP_E = IarIncE; IM_OV_E = ImOvE; INC_IAR_TMP_DATA_S = ADD_1_DATA; ALU_INS = IR_input[10];
  //   RE_OV_E = ReOvE; RESET_FLG = RstFlg; SET_FLG = SetFlg; STEP_1 = IAR_TMP_S

  // Notes on the sheet:
  //   Enabling section
  //   Enabling registers
  //   REG A
  //   REG B
  //   Setting flag
  //   Stepper
  //   contents of ROM (hex, n*v repeats v):
  //   22 11 66 13*0 44 32 32 22 46 22 38 75 95 8*0 15 47 15 0 16 49 5a 8a 7*0 33 0 0 66
  //   in current step
  //   What to set and what to enable
  //   Choosing a control section instruction
  //   REG B
  //   REG A
  //   Setting section
  //   Registers setting
endmodule
