// Logisim project alu3_5v2.circ as structural Verilog: 12 circuits, main circuit ADDER8bit
module ADDER8bit (
  input  CIN,
  input  [10:0] ARG1,
  input  [10:0] ARG2,
  output [10:0] RESULT,
  output COUT
);

  Adder #(.width(11)) adder_1 (.a(ARG1), .b(ARG2), .out(RESULT), .cin(CIN), .cout(COUT));
endmodule

module ADDER_RE_IM (
  input  [10:0] A,
  input  [10:0] B,
  input  [10:0] C,
  input  [10:0] D,
  input  CIN_RE,
  input  CIN_IM,
  output [10:0] RESULT_REAL,
  output COUT_RE,
  output [10:0] RESULT_IM,
  output COUT_IM
);

  ADDER8bit adder8bit_1 (.ARG1(A), .ARG2(C), .RESULT(RESULT_REAL), .COUT(COUT_RE), .CIN(CIN_RE));
  ADDER8bit adder8bit_2 (.ARG1(B), .ARG2(D), .RESULT(RESULT_IM), .COUT(COUT_IM), .CIN(CIN_IM));
endmodule

module SUB8bit (
  input  CIN,
  input  [10:0] ARG1,
  input  [10:0] ARG2,
  output [10:0] RESULT,
  output COUT
);

  Subtractor #(.width(11)) subtractor_1 (.a(ARG1), .b(ARG2), .out(RESULT), .bin(CIN), .bout(COUT));
endmodule

module SUB_RE_IM (
  input  [10:0] A,
  input  [10:0] B,
  input  [10:0] C,
  input  [10:0] D,
  input  CIN_RE,
  input  CIN_IM,
  output [10:0] RESULT_REAL,
  output COUT_RE,
  output [10:0] RESULT_IM,
  output COUT_IM
);

  SUB8bit sub8bit_1 (.ARG1(A), .ARG2(C), .RESULT(RESULT_REAL), .COUT(COUT_RE), .CIN(CIN_RE));
  SUB8bit sub8bit_2 (.ARG1(B), .ARG2(D), .RESULT(RESULT_IM), .COUT(COUT_IM), .CIN(CIN_IM));
endmodule

module MULT_RE_IM (
  input  [10:0] A,
  input  [10:0] B,
  input  [10:0] C,
  input  [10:0] D,
  output [10:0] RESULT_HIGH_RE,
  output [10:0] RESULT_REAL,
  output REAL_OV,
  output [10:0] RESULT_IM,
  output IMAG_OV,
  output [10:0] HIGH_RESULT_IM
);

  wire adder_1_cout, adder_2_cout, subtractor_1_bout, subtractor_2_bout;
  wire [10:0] multiplier_1_cout, multiplier_1_out, multiplier_2_cout, multiplier_2_out, multiplier_3_cout,
       multiplier_3_out, multiplier_4_cout, multiplier_4_out;

  Multiplier #(.width(11)) multiplier_1 (.a(A), .b(C), .out(multiplier_1_out), .cout(multiplier_1_cout));  // open: cin
  Multiplier #(.width(11)) multiplier_2 (.a(B), .b(D), .out(multiplier_2_out), .cout(multiplier_2_cout));  // open: cin
  Multiplier #(.width(11)) multiplier_3 (.a(B), .b(C), .out(multiplier_3_out), .cout(multiplier_3_cout));  // open: cin
  Multiplier #(.width(11)) multiplier_4 (.a(A), .b(D), .out(multiplier_4_out), .cout(multiplier_4_cout));  // open: cin
  Subtractor #(.width(11)) subtractor_1 (
    .a(multiplier_1_out), .b(multiplier_2_out), .out(RESULT_REAL), .bout(subtractor_1_bout));  // open: bin
  Subtractor #(.width(11)) subtractor_2 (
    .a(multiplier_1_cout), .b(multiplier_2_cout), .out(RESULT_HIGH_RE), .bin(subtractor_1_bout),
    .bout(subtractor_2_bout));
  Adder #(.width(11)) adder_1 (
    .a(multiplier_3_out), .b(multiplier_4_out), .out(RESULT_IM), .cout(adder_1_cout));  // open: cin
  Adder #(.width(11)) adder_2 (
    .a(multiplier_3_cout), .b(multiplier_4_cout), .out(HIGH_RESULT_IM), .cin(adder_1_cout),
    .cout(adder_2_cout));
  or or_1 (REAL_OV, RESULT_HIGH_RE[5], RESULT_HIGH_RE[0], RESULT_HIGH_RE[1], RESULT_HIGH_RE[2], RESULT_HIGH_RE[3], RESULT_HIGH_RE[4], RESULT_HIGH_RE[6], RESULT_HIGH_RE[7], RESULT_HIGH_RE[8], RESULT_HIGH_RE[9], RESULT_HIGH_RE[10], subtractor_2_bout);
  or or_2 (IMAG_OV, HIGH_RESULT_IM[0], HIGH_RESULT_IM[1], HIGH_RESULT_IM[2], HIGH_RESULT_IM[3], HIGH_RESULT_IM[4], HIGH_RESULT_IM[5], HIGH_RESULT_IM[6], HIGH_RESULT_IM[7], HIGH_RESULT_IM[8], HIGH_RESULT_IM[9], HIGH_RESULT_IM[10], adder_2_cout);

  // Other names for the same wires on the sheet: A_t[10:0] = A; B_t[10:0] = B; C_t[10:0] = C; D_t[10:0] = D

  // Notes on the sheet:
  //   wszystko wedle wzoru : (ac-bd)+(bc+ad)i
  //   (ac)
  //   (bd)
  //   bc
  //   ad
  //   (starsze bity)
  //   (starsze bity)
  //   (starsze bity)
  //   (starsze bity)
  //   (ac-bd)
endmodule

module DIV_RE_IM (
  input  [10:0] A,
  input  [10:0] B,
  input  [10:0] C,
  input  [10:0] D,
  output [10:0] RESULT_REAL,
  output REAL_OV,
  output DIV_0_error,
  output [10:0] RESULT_IM,
  output IMAG_OV
);

  wire adder_1_cout, adder_3_cout, subtractor_1_bout;
  wire [10:0] adder_1_out, adder_2_out, adder_3_out, adder_4_out, multiplier_1_cout, multiplier_1_out,
       multiplier_2_cout, multiplier_2_out, multiplier_3_cout, multiplier_3_out, multiplier_4_cout,
       multiplier_4_out, multiplier_5_cout, multiplier_5_out, multiplier_6_cout, multiplier_6_out,
       subtractor_1_out, subtractor_2_out;
  wire [22:0] divider_1_rem, divider_2_rem;
  wire [22:11] divider_1_out, divider_2_out;
  wire [22:22] adder_2_cout, adder_4_cout, subtractor_2_bout;

  Multiplier #(.width(11)) multiplier_1 (.a(A), .b(C), .out(multiplier_1_out), .cout(multiplier_1_cout));  // open: cin
  Multiplier #(.width(11)) multiplier_2 (.a(B), .b(D), .out(multiplier_2_out), .cout(multiplier_2_cout));  // open: cin
  Multiplier #(.width(11)) multiplier_3 (.a(C), .b(C), .out(multiplier_3_out), .cout(multiplier_3_cout));  // open: cin
  Multiplier #(.width(11)) multiplier_4 (.a(D), .b(D), .out(multiplier_4_out), .cout(multiplier_4_cout));  // open: cin
  Multiplier #(.width(11)) multiplier_5 (.a(B), .b(C), .out(multiplier_5_out), .cout(multiplier_5_cout));  // open: cin
  Multiplier #(.width(11)) multiplier_6 (.a(A), .b(D), .out(multiplier_6_out), .cout(multiplier_6_cout));  // open: cin
  Adder #(.width(11)) adder_1 (
    .a(multiplier_1_out), .b(multiplier_2_out), .out(adder_1_out), .cout(adder_1_cout));  // open: cin
  Adder #(.width(11)) adder_2 (
    .a(multiplier_1_cout), .b(multiplier_2_cout), .out(adder_2_out), .cin(adder_1_cout),
    .cout(adder_2_cout[22]));
  Adder #(.width(11)) adder_3 (
    .a(multiplier_3_out), .b(multiplier_4_out), .out(adder_3_out), .cout(adder_3_cout));  // open: cin
  Adder #(.width(11)) adder_4 (
    .a(multiplier_3_cout), .b(multiplier_4_cout), .out(adder_4_out), .cin(adder_3_cout),
    .cout(adder_4_cout[22]));
  Subtractor #(.width(11)) subtractor_1 (
    .a(multiplier_5_out), .b(multiplier_6_out), .out(subtractor_1_out), .bout(subtractor_1_bout));  // open: bin
  Subtractor #(.width(11)) subtractor_2 (
    .a(multiplier_5_cout), .b(multiplier_6_cout), .out(subtractor_2_out), .bin(subtractor_1_bout),
    .bout(subtractor_2_bout[22]));
  Divider #(.width(23)) divider_1 (
    .a({subtractor_2_bout[22], subtractor_2_out, subtractor_1_out}),
    .b({adder_4_cout[22], adder_4_out, adder_3_out}), .out({divider_1_out, RESULT_IM}), .rem(divider_1_rem));  // open: upper
  Divider #(.width(23)) divider_2 (
    .a({adder_2_cout[22], adder_2_out, adder_1_out}), .b({adder_4_cout[22], adder_4_out, adder_3_out}),
    .out({divider_2_out, RESULT_REAL}), .rem(divider_2_rem));  // open: upper
  nor nor_1 (DIV_0_error, adder_3_out[0], adder_3_out[1], adder_3_out[2], adder_3_out[3], adder_3_out[4], adder_3_out[5], adder_3_out[6], adder_3_out[7], adder_3_out[8], adder_3_out[9], adder_3_out[10], adder_4_out[0], adder_4_out[1], adder_4_out[2], adder_4_out[3], adder_4_out[4], adder_4_out[5], adder_4_out[6], adder_4_out[7], adder_4_out[8], adder_4_out[9], adder_4_out[10], adder_4_cout[22]);
  or or_1 (REAL_OV, divider_2_out[22], divider_2_out[11], divider_2_out[12], divider_2_out[13], divider_2_out[14], divider_2_out[15], divider_2_out[16], divider_2_out[17], divider_2_out[18], divider_2_out[19], divider_2_out[20], divider_2_out[21]);
  or or_2 (IMAG_OV, divider_1_out[22], divider_1_out[11], divider_1_out[12], divider_1_out[13], divider_1_out[14], divider_1_out[15], divider_1_out[16], divider_1_out[17], divider_1_out[18], divider_1_out[19], divider_1_out[20], divider_1_out[21]);

  // Other names for the same wires on the sheet: A_t[10:0] = A; B_t[10:0] = B; C_t[10:0] = C; D_t[10:0] = D

  // Notes on the sheet:
  //   (ac)
  //   (bd)
  //   wedle wzoru (ac+bd)/(c^2 +d^2)
  //   (ac)
  //   (starsze bity)
  //   (bd)
  //   (starsze bity)
  //   (bd)
  //   (starsze bity)
  //   (starsze bity)
  //   (starsze bity)
  //   (starsze bity)
  //   komentarz: co zrobic z resztami? czy 15 bitow to dobre rozwiazanie?
  //   (bc-ad)
  //   (bc-ad)/(c^2+d^2)
  //   (ac+bd)
  //   (c^2+d^2)
  //   reszta
  //   reszta
  //   result_im_high_bits
  //   result_real_high_bits
endmodule

module ALU_v2 (
  input  CIN_RE,
  input  CIN_IM,
  input  [10:0] A,
  input  [10:0] B,
  input  [10:0] C,
  input  [10:0] D,
  input  [3:0] OPERATION,
  output [10:0] RESULT_A,
  output [10:0] RESULT_B,
  output COUT_RE,
  output COUT_IM,
  output AisHigherThanCFLAG,
  output DIV_BY_0,
  output AequalsCFLAG,
  output A_B_equals_C_D,
  output [10:0] HIGH_BITS_REAL,
  output [10:0] HIGH_BITS_IMAG,
  output isZeroInAFlag
);

  wire A_is_less_than_0, adder_1_cout, adder_re_im_1_cout_im, adder_re_im_1_cout_re, AequalsB, AisHigher,
       BisHigher, comparatora_bv2_3_arowneb, div_re_im_1_div_0_error, div_re_im_1_imag_ov,
       div_re_im_1_real_ov, incr_OV_11, mult_re_im_1_imag_ov, mult_re_im_1_real_ov, OV_MOD_22, OV_MOD_A_B,
       sub_re_im_1_cout_im, sub_re_im_1_cout_re;
  wire [10:0] A_minus_1, A_plus_1, adder_re_im_1_result_im, adder_re_im_1_result_real, AdivC_result, AxC_ov,
       AxCresult, div_re_im_1_result_im, div_re_im_1_result_real, fil_incr, higher_mod_A_B, mod_A_B,
       mult_re_im_1_high_result_im, mult_re_im_1_result_high_re, mult_re_im_1_result_im,
       mult_re_im_1_result_real, sub_re_im_1_result_im, sub_re_im_1_result_real;

  ADDER_RE_IM adder_re_im_1 (
    .RESULT_REAL(adder_re_im_1_result_real), .COUT_RE(adder_re_im_1_cout_re),
    .RESULT_IM(adder_re_im_1_result_im), .COUT_IM(adder_re_im_1_cout_im), .A(A), .B(B), .C(C), .D(D),
    .CIN_RE(CIN_RE), .CIN_IM(CIN_IM));
  SUB_RE_IM sub_re_im_1 (
    .RESULT_REAL(sub_re_im_1_result_real), .COUT_RE(sub_re_im_1_cout_re), .RESULT_IM(sub_re_im_1_result_im),
    .COUT_IM(sub_re_im_1_cout_im), .A(A), .B(B), .C(C), .D(D), .CIN_RE(CIN_RE), .CIN_IM(CIN_IM));
  comparatorA_Bv2 comparatora_bv2_1 (
    .AmniejszeB(BisHigher), .ArowneB(AequalsB), .AwiekszeB(AisHigher), .in_1(A), .in_2(B));
  MULT_RE_IM mult_re_im_1 (
    .RESULT_REAL(mult_re_im_1_result_real), .REAL_OV(mult_re_im_1_real_ov),
    .RESULT_IM(mult_re_im_1_result_im), .IMAG_OV(mult_re_im_1_imag_ov), .A(A), .B(B), .C(C), .D(D),
    .RESULT_HIGH_RE(mult_re_im_1_result_high_re), .HIGH_RESULT_IM(mult_re_im_1_high_result_im));
  DIV_RE_IM div_re_im_1 (
    .RESULT_REAL(div_re_im_1_result_real), .REAL_OV(div_re_im_1_real_ov),
    .DIV_0_error(div_re_im_1_div_0_error), .RESULT_IM(div_re_im_1_result_im), .IMAG_OV(div_re_im_1_imag_ov),
    .A(A), .B(B), .C(C), .D(D));
  moduleReIm modulereim_1 (
    .MODULE(mod_A_B), .OV_mod(OV_MOD_A_B), .in_1(A), .in_2(B), .MODULE_higher(higher_mod_A_B),
    .OV_higher_mod(OV_MOD_22));
  nor nor_1 (isZeroInAFlag, A[0], A[1], A[2], A[3], A[4], A[5], A[6], A[7], A[8], A[9], A[10]);
  decrementer decrementer_1 (.A_minus_1(A_minus_1), .care(A_is_less_than_0), .in_1(A));
  Multiplexer #(.select(4), .width(11), .enable("false")) multiplexer_1 (
    .in0(fil_incr), .in1(adder_re_im_1_result_real), .in2(sub_re_im_1_result_real),
    .in3(mult_re_im_1_result_real), .in4(div_re_im_1_result_real), .in5(mod_A_B), .in7(A_minus_1),
    .in8(A_plus_1), .in9(AxCresult), .in10(AdivC_result), .out(RESULT_A), .sel(OPERATION));  // open: in6, in11, in12, in13, in14, in15
  Multiplexer #(.select(4), .enable("false")) multiplexer_2 (
    .in0(adder_1_cout), .in1(adder_re_im_1_cout_re), .in2(sub_re_im_1_cout_re), .in3(mult_re_im_1_real_ov),
    .in4(div_re_im_1_real_ov), .in5(OV_MOD_A_B), .in6(AisHigher), .in7(A_is_less_than_0), .in8(incr_OV_11),
    .in9(1'b0), .in10(1'b0), .in11(1'b0), .in12(1'b0), .in13(1'b0), .in14(1'b0), .in15(1'b0), .out(COUT_RE),
    .sel(OPERATION));
  Multiplexer #(.select(4), .enable("false")) multiplexer_3 (
    .in0(1'b0), .in1(1'b0), .in2(1'b0), .in3(1'b0), .in4(div_re_im_1_div_0_error), .in5(1'b0), .in6(1'b0),
    .in7(1'b0), .in8(1'b0), .in9(1'b0), .in10(1'b0), .in11(1'b0), .in12(1'b0), .in13(1'b0), .in14(1'b0),
    .in15(1'b0), .out(DIV_BY_0), .sel(OPERATION));
  Multiplexer #(.select(4), .enable("false")) multiplexer_4 (
    .in0(1'b0), .in1(adder_re_im_1_cout_im), .in2(sub_re_im_1_cout_im), .in3(mult_re_im_1_imag_ov),
    .in4(div_re_im_1_imag_ov), .in5(OV_MOD_22), .in6(BisHigher), .in7(1'b0), .in8(1'b0), .in9(1'b0),
    .in10(1'b0), .in11(1'b0), .in12(1'b0), .in13(1'b0), .in14(1'b0), .in15(1'b0), .out(COUT_IM),
    .sel(OPERATION));
  incrementer incrementer_1 (.A_plus_1(A_plus_1), .care(incr_OV_11), .in_1(A));
  Multiplexer #(.select(4), .width(11), .enable("false")) multiplexer_5 (
    .in1(adder_re_im_1_result_im), .in2(sub_re_im_1_result_im), .in3(mult_re_im_1_result_im),
    .in4(div_re_im_1_result_im), .in5(higher_mod_A_B), .out(RESULT_B), .sel(OPERATION));  // open: in0, in6, in7, in8, in9, in10, in11, in12, in13, in14, in15
  Multiplexer #(.select(4), .width(11), .enable("false")) multiplexer_6 (
    .in3(mult_re_im_1_high_result_im), .out(HIGH_BITS_IMAG), .sel(OPERATION));  // open: in0, in1, in2, in4, in5, in6, in7, in8, in9, in10, in11, in12, in13, in14, in15
  Multiplexer #(.select(4), .width(11), .enable("false")) multiplexer_7 (
    .in3(mult_re_im_1_result_high_re), .in9(AxC_ov), .out(HIGH_BITS_REAL), .sel(OPERATION));  // open: in0, in1, in2, in4, in5, in6, in7, in8, in10, in11, in12, in13, in14, in15
  Adder #(.width(11)) adder_1 (.a(A), .b(C), .out(fil_incr), .cout(adder_1_cout));  // open: cin
  comparatorA_Bv2 comparatora_bv2_2 (
    .ArowneB(AequalsCFLAG), .AwiekszeB(AisHigherThanCFLAG), .in_1(A), .in_2(C));  // open: AmniejszeB
  Multiplier #(.width(11)) multiplier_1 (.a(A), .b(C), .out(AxCresult), .cout(AxC_ov));  // open: cin
  Divider #(.width(11)) divider_1 (.a(A), .b(C), .out(AdivC_result));  // open: upper, rem
  and and_1 (A_B_equals_C_D, AequalsCFLAG, comparatora_bv2_3_arowneb);
  comparatorA_Bv2 comparatora_bv2_3 (
    .ArowneB(comparatora_bv2_3_arowneb), .in_1(B), .in_2(D));  // open: AmniejszeB, AwiekszeB

  // Other names for the same wires on the sheet: cin_im_t = CIN_IM; cin_re_t = CIN_RE; im1_t[10:0] = B;
  //   im2_t[10:0] = D; ins_code[3:0] = OPERATION; re1_t[10:0] = A; re2_t[10:0] = C

  // Notes on the sheet:
  //   nieużywane chwilowo
  //   pierwsza liczba
  //   A-re, B-im
  //   0110-porownanie liczby A i liczby B
  //   sprawdz czy liczba w rejestrze A jest rowna 0
  //   0101-moduł z REAL1(A) i imagq(B)
  //   C-re, D-im
  //   druga liczba
  //   (wartosc 1(true) kiedy w A jest 0
  //   nieużywane
  //   0111-pommniejszenie wartosci liczby A o 1
  //   wybór operacji
  //   0001- dodawanie
  //   0010 - odejmowanie
  //   0011- mnozenie
  //   0100- dzielenie
  //   0000- dodanie liczby A+C, zapis do RESULT_A, nadmiar w cout_RE
  //   0101-moduł z REAL1(A) i imagq(B)
  //   0110-porownanie liczby A i liczby C
  //   0111-pommniejszenie wartosci liczby A o 1
  //   1000-powieksznie wartosci liczby A o 1
  //   1010-podzielenie (calkowite) A/C wynik w RESULT_A
  //   1000-powieksznie wartosci liczby A o 1
  //   isZeroInAFlag zwraca wartość true(1) kiedy w rejestrze A ALU otrzyma liczbę równą 0
  //   1001- pomnożenie A*C wynik w RESULT_A, starsze bity w HIGH_RE
  //   0000-operacja dodania liczby A i liczby B, zapis do RES_A
  //   0000- dodanie liczby A+B, zapis do RESULT_A
  //   starsze bity czesci rzeczywistej po operacji mnozenia
  //   starsze bity czesci urojonej po operacji mnozenia
  //   A
  //   dla podstawowych operacji:
  //   0101-moduł z REAL1(A) i imagq(B)
  //   0110-porownanie liczby A i liczby C
  //   CoutRE- 1(true) jesli A<C
  //   CoutIM- 1(true) jesli A>C
  //   CoutIm, CoutRE ==0(false) A==C
  //   C
  //   analogicznie result_B to czesc urojona wyniku
  //   coutIM swiadczy o nadmiarze w czesci urojonej (1- jest nadmiar)
  //   do RESULT_A zapisuję 11 najmlodszych bitow modulu
  //   do RESULT_B zapisuje 22-11 bity modułu( czesc starsza)
  //   1001- pomnożenie A*C wynik w RESULT_A, starsze bity w HIGH_RE
  //   1010-podzielenie (calkowite) A/C wynik w RESULT_A
  //   ALU przyjmuje dwie liczby w postaci A,B i C,D, gdzie A to real1 B imag1, C real2, Dimag2
  //   wyjscia: result_A to czesc realna wyniku(dodawania,mnozenia,dzielenia,odejmowania)
  //   coutRE swidczy o nadmiarze w czesci rzeczywistej (1-true-jest nadmiar)
  //   w coutRE jest informacja(true(1), false(0) czy wynik potrzebuje wiecej niz 11bitow(czy jest wiekszy niz 11bit)
  //   w coutIM jest informacja czy wynik jest wiekszy niz 22 bity(nie mamy juz tego nadmiaru w żadnym rejestrze)
  //   B
  //   D
  //   0111-pommniejszenie wartosci liczby A o 1
  //   1000-powieksznie wartosci liczby A o 1
  //   FLAGI
  //   Bierze liczbę z podanego na wejście A, odejmuje 1, zwracado RESULT_A
  //   Jeśli otrzymana liczba bedzie ujemna, cout_RE zostanie ustawione na true(1)
  //   UWAGA! isZeroFlag jest sprawdzana dla A na wejsciu, a nie dla RESULT_A
  //   Bierze liczbę z podanego na wejście A, dodaje 1, zwracado RESULT_A
  //   UWAGA! isZeroFlag jest sprawdzana dla A na wejsciu, a nie dla RESULT_A
  //   Jeśli otrzymana liczba bedzie wieksza niz 11bit, cout_RE zostanie ustawione na true(1)
endmodule

module moduleReIm (
  input  [10:0] in_1,
  input  [10:0] in_2,
  output [10:0] MODULE,
  output [10:0] MODULE_higher,
  output OV_mod,
  output OV_higher_mod
);

  wire adder_1_cout;
  wire [10:0] multiplier_1_cout, multiplier_1_out, multiplier_2_cout, multiplier_2_out;

  Multiplier #(.width(11)) multiplier_1 (
    .a(in_1), .b(in_1), .out(multiplier_1_out), .cout(multiplier_1_cout));  // open: cin
  Multiplier #(.width(11)) multiplier_2 (
    .a(in_2), .b(in_2), .out(multiplier_2_out), .cout(multiplier_2_cout));  // open: cin
  Adder #(.width(11)) adder_1 (
    .a(multiplier_1_out), .b(multiplier_2_out), .out(MODULE), .cout(adder_1_cout));  // open: cin
  Adder #(.width(11)) adder_2 (
    .a(multiplier_1_cout), .b(multiplier_2_cout), .out(MODULE_higher), .cin(adder_1_cout),
    .cout(OV_higher_mod));
  or or_1 (OV_mod, MODULE_higher[0], MODULE_higher[1], MODULE_higher[2], MODULE_higher[3], MODULE_higher[4], MODULE_higher[5], MODULE_higher[6], MODULE_higher[7], MODULE_higher[8], MODULE_higher[9], MODULE_higher[10], OV_higher_mod);

  // Other names for the same wires on the sheet: part_a[10:0] = in_1; part_b[10:0] = in_2

  // Notes on the sheet:
  //   real
  //   a*a
  //   starsze bity
  //   b*b
  //   starsze bity
  //   imaginary
  //   (a^2)+(b^2)
  //   wyzsze bity modulu
endmodule

module comparatorA_B (
  input  [10:0] in_1,
  input  [10:0] in_2,
  output AwiekszeOdB,
  output AmniejszeOdB,
  output ArowneB
);

  wire A_mniejsze_OD_B_2_out, A_mniejsze_OD_B_3_out, A_mniejsze_OD_B_4_out, A_mniejsze_OD_B_5_out,
       A_mniejsze_OD_B_6_out, A_mniejsze_OD_B_7_out, A_mniejsze_OD_B_8_out, A_mniejsze_OD_B_9_out,
       A_mniejsze_OD_B_10_out, A_mniejsze_OD_B_11_out, A_ROWNE_B_2_out, A_ROWNE_B_3_out, A_ROWNE_B_4_out,
       A_ROWNE_B_5_out, A_ROWNE_B_6_out, A_ROWNE_B_7_out, A_ROWNE_B_8_out, A_ROWNE_B_9_out, A_ROWNE_B_10_out,
       A_ROWNE_B_11_out, A_ROWNE_B_out, A_WIEKSZE_ODB_2_out, A_WIEKSZE_ODB_3_out, A_WIEKSZE_ODB_4_out,
       A_WIEKSZE_ODB_5_out, A_WIEKSZE_ODB_6_out, A_WIEKSZE_ODB_7_out, A_WIEKSZE_ODB_8_out,
       A_WIEKSZE_ODB_9_out, A_WIEKSZE_ODB_10_out, A_WIEKSZE_ODB_11_out, AmB1, AmB2, AmB3, AmB4, AmB5, AmB6,
       AmB7, AmB8, AmB9, AmB10, AmB11, and_3_out, and_22_out, and_23_out, and_24_out, and_25_out, and_26_out,
       and_27_out, and_28_out, and_29_out, AwB1, AwB2, AwB3, AwB4, AwB5, AwB6, AwB7, AwB8, AwB9, AwB10,
       AwB11, not_1_out, not_2_out, not_3_out, not_4_out, not_5_out, not_6_out, not_7_out, not_8_out,
       not_9_out, not_10_out, not_11_out, not_12_out, not_13_out, not_14_out, not_15_out, not_16_out,
       not_17_out, not_18_out, not_19_out, not_20_out, not_21_out, not_22_out;

  not not_1 (not_1_out, in_1[10]);
  not not_2 (not_2_out, in_2[10]);
  and A_mniejsze_OD_B (AmB11, not_1_out, in_2[10]);
  and A_WIEKSZE_ODB (AwB11, in_1[10], not_2_out);
  xnor A_ROWNE_B (A_ROWNE_B_out, in_1[10], in_2[10]);
  not not_3 (not_3_out, in_1[9]);
  and A_mniejsze_OD_B_2 (A_mniejsze_OD_B_2_out, not_3_out, in_2[9]);
  and A_WIEKSZE_ODB_2 (A_WIEKSZE_ODB_2_out, in_1[9], not_4_out);
  not not_4 (not_4_out, in_2[9]);
  xnor A_ROWNE_B_2 (A_ROWNE_B_2_out, in_1[9], in_2[9]);
  not not_5 (not_5_out, in_1[8]);
  and A_mniejsze_OD_B_3 (A_mniejsze_OD_B_3_out, not_5_out, in_2[8]);
  and A_WIEKSZE_ODB_3 (A_WIEKSZE_ODB_3_out, in_1[8], not_6_out);
  not not_6 (not_6_out, in_2[8]);
  xnor A_ROWNE_B_3 (A_ROWNE_B_3_out, in_1[8], in_2[8]);
  not not_7 (not_7_out, in_1[7]);
  and A_mniejsze_OD_B_4 (A_mniejsze_OD_B_4_out, not_7_out, in_2[7]);
  and A_WIEKSZE_ODB_4 (A_WIEKSZE_ODB_4_out, in_1[7], not_8_out);
  not not_8 (not_8_out, in_2[7]);
  xnor A_ROWNE_B_4 (A_ROWNE_B_4_out, in_1[7], in_2[7]);
  not not_9 (not_9_out, in_1[6]);
  and A_mniejsze_OD_B_5 (A_mniejsze_OD_B_5_out, not_9_out, in_2[6]);
  and A_WIEKSZE_ODB_5 (A_WIEKSZE_ODB_5_out, in_1[6], not_10_out);
  not not_10 (not_10_out, in_2[6]);
  xnor A_ROWNE_B_5 (A_ROWNE_B_5_out, in_1[6], in_2[6]);
  not not_11 (not_11_out, in_1[5]);
  and A_mniejsze_OD_B_6 (A_mniejsze_OD_B_6_out, not_11_out, in_2[5]);
  and A_WIEKSZE_ODB_6 (A_WIEKSZE_ODB_6_out, in_1[5], not_12_out);
  not not_12 (not_12_out, in_2[5]);
  xnor A_ROWNE_B_6 (A_ROWNE_B_6_out, in_1[5], in_2[5]);
  not not_13 (not_13_out, in_1[4]);
  and A_mniejsze_OD_B_7 (A_mniejsze_OD_B_7_out, not_13_out, in_2[4]);
  and A_WIEKSZE_ODB_7 (A_WIEKSZE_ODB_7_out, in_1[4], not_14_out);
  not not_14 (not_14_out, in_2[4]);
  xnor A_ROWNE_B_7 (A_ROWNE_B_7_out, in_1[4], in_2[4]);
  not not_15 (not_15_out, in_1[3]);
  and A_mniejsze_OD_B_8 (A_mniejsze_OD_B_8_out, not_15_out, in_2[3]);
  and A_WIEKSZE_ODB_8 (A_WIEKSZE_ODB_8_out, in_1[3], not_16_out);
  not not_16 (not_16_out, in_2[3]);
  xnor A_ROWNE_B_8 (A_ROWNE_B_8_out, in_1[3], in_2[3]);
  not not_17 (not_17_out, in_1[2]);
  and A_mniejsze_OD_B_9 (A_mniejsze_OD_B_9_out, not_17_out, in_2[2]);
  and A_WIEKSZE_ODB_9 (A_WIEKSZE_ODB_9_out, in_1[2], not_18_out);
  not not_18 (not_18_out, in_2[2]);
  xnor A_ROWNE_B_9 (A_ROWNE_B_9_out, in_1[2], in_2[2]);
  not not_19 (not_19_out, in_1[1]);
  and A_mniejsze_OD_B_10 (A_mniejsze_OD_B_10_out, not_19_out, in_2[1]);
  and A_WIEKSZE_ODB_10 (A_WIEKSZE_ODB_10_out, in_1[1], not_20_out);
  not not_20 (not_20_out, in_2[1]);
  xnor A_ROWNE_B_10 (A_ROWNE_B_10_out, in_1[1], in_2[1]);
  not not_21 (not_21_out, in_1[0]);
  and A_mniejsze_OD_B_11 (A_mniejsze_OD_B_11_out, not_21_out, in_2[0]);
  and A_WIEKSZE_ODB_11 (A_WIEKSZE_ODB_11_out, in_1[0], not_22_out);
  not not_22 (not_22_out, in_2[0]);
  xnor A_ROWNE_B_11 (A_ROWNE_B_11_out, in_1[0], in_2[0]);
  and and_1 (AmB10, A_ROWNE_B_out, A_mniejsze_OD_B_2_out);
  and and_2 (AwB10, A_WIEKSZE_ODB_2_out, A_ROWNE_B_out);
  and and_3 (and_3_out, A_ROWNE_B_out, A_ROWNE_B_2_out);
  and and_4 (AmB9, and_3_out, A_mniejsze_OD_B_3_out);
  and and_5 (AwB9, A_WIEKSZE_ODB_3_out, and_3_out);
  and and_6 (AmB8, and_22_out, A_mniejsze_OD_B_4_out);
  and and_7 (AwB8, A_WIEKSZE_ODB_4_out, and_22_out);
  and and_8 (AmB7, and_23_out, A_mniejsze_OD_B_5_out);
  and and_9 (AwB7, A_WIEKSZE_ODB_5_out, and_23_out);
  and and_10 (AmB6, and_24_out, A_mniejsze_OD_B_6_out);
  and and_11 (AwB6, A_WIEKSZE_ODB_6_out, and_24_out);
  and and_12 (AmB5, and_25_out, A_mniejsze_OD_B_7_out);
  and and_13 (AwB5, A_WIEKSZE_ODB_7_out, and_25_out);
  and and_14 (AmB4, and_26_out, A_mniejsze_OD_B_8_out);
  and and_15 (AwB4, A_WIEKSZE_ODB_8_out, and_26_out);
  and and_16 (AmB3, and_27_out, A_mniejsze_OD_B_9_out);
  and and_17 (AwB3, A_WIEKSZE_ODB_9_out, and_27_out);
  and and_18 (AmB2, and_28_out, A_mniejsze_OD_B_10_out);
  and and_19 (AwB2, A_WIEKSZE_ODB_10_out, and_28_out);
  and and_20 (AmB1, and_29_out, A_mniejsze_OD_B_11_out);
  and and_21 (AwB1, A_WIEKSZE_ODB_11_out, and_29_out);
  or or_1 (AmniejszeOdB, AmB11, AmB10, AmB9, AmB8, AmB7, AmB6, AmB5, AmB4, AmB3, AmB2, AmB1);
  and and_22 (and_22_out, and_3_out, A_ROWNE_B_3_out);
  and and_23 (and_23_out, and_22_out, A_ROWNE_B_4_out);
  and and_24 (and_24_out, and_23_out, A_ROWNE_B_5_out);
  and and_25 (and_25_out, and_24_out, A_ROWNE_B_6_out);
  and and_26 (and_26_out, and_25_out, A_ROWNE_B_7_out);
  and and_27 (and_27_out, and_26_out, A_ROWNE_B_8_out);
  and and_28 (and_28_out, and_27_out, A_ROWNE_B_9_out);
  and and_29 (and_29_out, and_28_out, A_ROWNE_B_10_out);
  and and_30 (ArowneB, and_29_out, A_ROWNE_B_11_out);
  or or_2 (AwiekszeOdB, AwB11, AwB10, AwB9, AwB8, AwB7, AwB6, AwB5, AwB4, AwB3, AwB2, AwB1);

  // Other names for the same wires on the sheet: ArowneB0 = ArowneB

  // Notes on the sheet:
  //   A
  //   B
endmodule

module comparatorA_Bv2 (
  input  [10:0] in_1,
  input  [10:0] in_2,
  output AmniejszeB,
  output ArowneB,
  output AwiekszeB
);

  Comparator #(.width(11)) comparator_1 (.a(in_2), .b(in_1), .gt(AmniejszeB), .eq(ArowneB), .lt(AwiekszeB));

  // Notes on the sheet:
  //   A
  //   B
endmodule

module decrementer (
  input  [10:0] in_1,
  output [10:0] A_minus_1,
  output care
);

  SUB8bit sub8bit_1 (.ARG1(in_1), .ARG2(11'h1), .RESULT(A_minus_1), .COUT(care));  // open: CIN

  // Notes on the sheet:
  //   "1"
  //   A
endmodule

module incrementer (
  input  [10:0] in_1,
  output [10:0] A_plus_1,
  output care
);

  ADDER8bit adder8bit_1 (.ARG1(in_1), .ARG2(11'h1), .RESULT(A_plus_1), .COUT(care));  // open: CIN

  // Notes on the sheet:
  //   "1"
  //   A
endmodule
